# Fritzing sketch FRITZIG 2 (saved by Fritzing 0.9.3b)
breadboards: 1

parts:
  VCC1 = Battery
  U1 = LM358 [package=dip08]
  R3 = Resistor [tolerance=±5% resistance=220 package=THT]
  R4 = Resistor [tolerance=±5% resistance=10k package=THT]
  R5 = Resistor [tolerance=±5% resistance=100 package=THT]
  SG1 = Buzzer 12mm [package=buzzer-12mm-ns-kit]
  LED1 = LED - 5mm [color="Red (633nm)" package="5 mm [THT]"]
  R6 = Rotary Potentiometer (Small) [maximum_resistance=100kΩ package=THT]
  LED2 = LED - 5mm [color="Infrared (940nm)" package="5 mm [THT]"]
  LED3 = LED - 5mm [color="Infrared (850nm)" package="5 mm [THT]"]

nets:
  N1: VCC1.-, U1.G$1_V-, R4.Pin_0, R5.Pin_1, SG1.2, LED1.cathode, R6.leg2
  N2: VCC1.+, U1.G$1_V+, R6.leg1, LED2.anode, LED3.anode
  N3: U1.G$1_OUT, R3.Pin_1, SG1.1
  N4: U1.G$1_-IN, R6.wiper
  N5: U1.G$1_+IN, R4.Pin_1, LED2.cathode
  N6: R3.Pin_0, LED1.anode
  N7: R5.Pin_0, LED3.cathode
