# Fritzing sketch fitzig 1 (saved by Fritzing 0.9.3b)
breadboards: 1

parts:
  U1 = 555 Timer [package="DIP8 [THT]"]
  R1 = Resistor [tolerance=±5% resistance=100 package=THT]
  R2 = Resistor [tolerance=±5% resistance=1k package=THT]
  R3 = Resistor [tolerance=±5% resistance=100 package=THT]
  R4 = Resistor [tolerance=±5% resistance=100k package=THT]
  LED1 = LED - 5mm [color="Red (633nm)" package="5 mm [THT]"]
  LED2 = LED - 5mm [color="Red (633nm)" package="5 mm [THT]"]
  C2 = Electrolytic Capacitor [capacitance=22µF package="100 mil [THT, electrolytic]"]
  C3 = Ceramic Capacitor [capacitance=10nF package="100 mil [THT, multilayer]"]

nets:
  N1: U1.Ground, R3.Pin_0, C2.-
  N2: U1.Trigger, U1.Threshold, C2.+
  N3: U1.Output, R1.Pin_1, LED2.anode
  N4: U1.Control_Voltage, C3.0
  N5: U1.Discharge, R2.Pin_1, R4.Pin_0, R4.Pin_1
  N6: U1.Vcc_Supply_Voltage, LED1.anode
  N7: R1.Pin_0, LED1.cathode
  N8: R2.Pin_0, C3.1
  N9: R3.Pin_1, LED2.cathode
